# Fritzing sketch scheme (saved by Fritzing 0.9.3b)

parts:
  LCD1 = LCD screen  # not connected
  LCM1602_IIC1 = LCM1602 IIC [part_number="LCM1602 IIC" chip_label="LCM1602 IIC" package="DIP (Dual Inline) [THT]"]
  Часть1 = Arduino Nano (Rev3.0)
  R1 = Photocell (LDR) [package=THT]
  R2 = Resistor [tolerance=±5% resistance=10k package=THT]  # not connected
  S1 = Pushbutton [package="[THT]"]
  S2 = Pushbutton [package="[THT]"]
  S3 = Pushbutton [package="[THT]"]
  J1 = Piezo Speaker  # not connected

nets:
  GND: LCM1602_IIC1.GND, Часть1.GND, S1.Pin_1, S1.Pin_2, S2.Pin_1, S2.Pin_2, S3.Pin_1, S3.Pin_2
  VCC: LCM1602_IIC1.VCC, Часть1.5V
  N1: LCM1602_IIC1.SDA, Часть1.A4
  N2: LCM1602_IIC1.SCL, Часть1.A5
  N3: LCM1602_IIC1.LED_A, Часть1.D3
  N4: Часть1.D2, S1.Pin_3, S1.Pin_4
  N5: Часть1.D4, S2.Pin_3, S2.Pin_4
  N6: Часть1.D5, S3.Pin_4
  N7: Часть1.A0, R1.pin_1

custom parts:
  LCM1602 IIC: I2C-Module to use a 1602 or 2004 LCD on with the wire.h libory Serial LCD Modul
