# Fritzing sketch talk_clock (saved by Fritzing 0.9.3b)

parts:
  Часть1 = Arduino Uno (Rev3)
  LCD1 = LCD screen
  S1 = Pushbutton [package="[THT]"]
  S2 = Pushbutton [package="[THT]"]
  S3 = Pushbutton [package="[THT]"]
  R1 = Resistor [tolerance=±5% resistance=1k package=THT]
  R2 = Resistor [tolerance=±5% resistance=1k package=THT]
  Часть2 = Real Time Clock Module - DS1307 RTC Breakout Board
  R3 = Resistor [tolerance=±5% resistance=1k package=THT]
  LCM1602_IIC1 = LCM1602 IIC [part_number="LCM1602 IIC" chip_label="LCM1602 IIC" package="DIP (Dual Inline) [THT]"]
  R4 = PHOTOCELL [package=photocell]
  R6 = Resistor [tolerance=±5% resistance=10k package="0402 [SMD]"]
  DFPlayer_Mini1 = DFPlayer MINI [package="DIP (Dual Inline) [THT]"]
  SP1 = SPEAKER [package=pcb_mount_speaker]
  R7 = Resistor [tolerance=±5% resistance=1k package=THT]
  R8 = Resistor [tolerance=±5% resistance=1k package=THT]

nets:
  N1: Часть1.A1, R4.P$1, R6.Pin_1
  N2: Часть1.A4/SDA, Часть2.SDA, LCM1602_IIC1.SDA
  N3: Часть1.A5/SCL, Часть2.SCL, LCM1602_IIC1.SCL
  N4: Часть1.D8, S2.Pin_1, S2.Pin_2, R3.Pin_1
  N5: Часть1.D11_PWM/MOSI, LCM1602_IIC1.LED_A
  N6: Часть1.D12/MISO, R8.Pin_0
  N7: Часть1.D13/SCK, R7.Pin_0
  N8: Часть1.D4, S3.Pin_1, S3.Pin_2, R1.Pin_1
  N9: Часть1.D7, S1.Pin_1, S1.Pin_2, R2.Pin_1
  VSS: LCD1.VSS, LCM1602_IIC1.VSS
  VDD: LCD1.VDD, LCM1602_IIC1.VDD
  N10: LCD1.V0, LCM1602_IIC1.V0
  N11: LCD1.RS, LCM1602_IIC1.RS
  N12: LCD1.R/W, LCM1602_IIC1.RW
  N13: LCD1.E, LCM1602_IIC1.E
  N14: LCD1.DB0, LCM1602_IIC1.D0
  N15: LCD1.DB1, LCM1602_IIC1.D1
  N16: LCD1.DB2, LCM1602_IIC1.D2
  N17: LCD1.DB3, LCM1602_IIC1.D3
  N18: LCD1.DB4, LCM1602_IIC1.D4
  N19: LCD1.DB5, LCM1602_IIC1.D5
  N20: LCD1.DB6, LCM1602_IIC1.D6
  N21: LCD1.DB7, LCM1602_IIC1.D7
  N22: LCD1.LED+, LCM1602_IIC1.A
  N23: LCD1.LED-, LCM1602_IIC1.K
  N24: R1.Pin_0, R2.Pin_0, R3.Pin_0
  GND: LCM1602_IIC1.GND, R6.Pin_0, DFPlayer_Mini1.GND
  N25: DFPlayer_Mini1.TX, R8.Pin_1
  N26: DFPlayer_Mini1.SPK1, SP1.-

custom parts:
  Real Time Clock Module - DS1307 RTC Breakout Board: This a custom designed module for the DS1307 Real Time Clock. The module comes fully assembled and pre-programmed with the current time (ok, so it's our current time - MST). The included Lithium coin cell battery (CR1225 41mAh) will run the module for a minimum of 9 years (17 years typical) without external 5V power. The DS1307 is accessed via the I2C protocol. We've written a test-bed to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
  LCM1602 IIC: I2C-Module to use a 1602 or 2004 LCD on with the wire.h libory Serial LCD Modul
  DFPlayer MINI: MP3 module by DFRobot.com for playing Music from an SD-Card. Supports WAV and MP3 files.
